// Logisim project 11-systemy-cyfrowe.circ as structural Verilog: 2 circuits, main circuit iloczyn-nkb
module iloczyn_nkb (
  input  SYNC,
  input  [3:0] \Mnożnik ,
  input  [3:0] \Mnożna ,
  output ACK,
  output [7:0] Iloczyn
);

  wire adder_1_cout, clock_1_out, Licznik_carry, multiplexer_2_out, not_1_out, not_2_out, not_3_out,
       or_1_out, RH_out;
  wire [2:0] counter_1_q, rom_1_data, rom_1_data_3;
  wire [3:0] adder_1_out, MN_q3, multiplexer_1_out;
  wire [6:3] rom_1_data_2;

  Clock clock_1 (.out(clock_1_out));
  Shift_Register #(.length(4)) RH (
    .shift(rom_1_data_2[5]), .in(adder_1_cout), .clk(clock_1_out), .out(RH_out), .load(rom_1_data_2[4]),
    .clr(rom_1_data_2[3]), .d0(adder_1_out[3]), .q0(Iloczyn[7]), .d1(adder_1_out[2]), .q1(Iloczyn[6]),
    .d2(adder_1_out[1]), .q2(Iloczyn[5]), .d3(adder_1_out[0]), .q3(Iloczyn[4]));
  Shift_Register #(.length(4)) MK (
    .shift(rom_1_data_2[5]), .in(RH_out), .clk(clock_1_out), .load(rom_1_data_2[3]), .clr(1'b0),
    .d0(\Mnożnik [3]), .q0(Iloczyn[3]), .d1(\Mnożnik [2]), .q1(Iloczyn[2]), .d2(\Mnożnik [1]),
    .q2(Iloczyn[1]), .d3(\Mnożnik [0]), .q3(Iloczyn[0]));  // open: out
  Adder #(.width(4)) adder_1 (
    .a(multiplexer_1_out), .b(Iloczyn[7:4]), .out(adder_1_out), .cout(adder_1_cout));  // open: cin
  Shift_Register #(.length(4)) MN (
    .shift(1'b0), .in(1'b0), .clk(clock_1_out), .load(rom_1_data_2[3]), .clr(1'b0), .d0(\Mnożna [3]),
    .q0(MN_q3[3]), .d1(\Mnożna [2]), .q1(MN_q3[2]), .d2(\Mnożna [1]), .q2(MN_q3[1]), .d3(\Mnożna [0]),
    .q3(MN_q3[0]));  // open: out
  Multiplexer #(.width(4), .enable("false")) multiplexer_1 (
    .in0(4'b0000), .in1(MN_q3), .out(multiplexer_1_out), .sel(Iloczyn[0]));
  or or_1 (or_1_out, rom_1_data_2[5], rom_1_data_2[3]);
  Counter #(.width(3), .max('h7)) Licznik (
    .load(or_1_out), .D(3'b100), .count(rom_1_data_2[5]), .carry(Licznik_carry), .clk(clock_1_out), .clr(1'b0));  // open: Q
  not not_1 (not_1_out, SYNC);
  Multiplexer #(.select(3), .enable("false")) multiplexer_2 (
    .in0(SYNC), .in1(not_1_out), .in2(Iloczyn[0]), .in3(Licznik_carry), .in4(1'b1), .in5(1'b0), .in6(1'b0),
    .in7(1'b0), .out(multiplexer_2_out), .sel(rom_1_data_3));
  D_Flip_Flop d_ff_1 (
    .clk(1'b0), .D(1'b0), .Q(ACK), .preset(rom_1_data_2[6]), .en(1'b0), .reset(rom_1_data_2[3]));  // open: Qn
  not not_2 (not_2_out, multiplexer_2_out);
  Counter #(.width(3), .max('h7)) counter_1 (
    .load(not_2_out), .D(rom_1_data), .count(multiplexer_2_out), .Q(counter_1_q), .clk(not_3_out));  // open: carry, clr
  not not_3 (not_3_out, clock_1_out);
  ROM #(.addrWidth(3), .dataWidth(10)) rom_1 (
    .addr(counter_1_q), .data({rom_1_data_3, rom_1_data_2, rom_1_data}));  // open: sel

  // Notes on the sheet:
  //   S0
  //   S1
  //   S2
  //   S3
  //   MK0
  //   contents of rom_1 (hex, n*v repeats v):
  //   8 103 210 1a1 c4 280
endmodule

module suma_szeregowe_wejscie (
  input  SYNC,
  input  [3:0] A,
  input  [3:0] B,
  output ACK,
  output OUT
);

  wire CK_out, LY_carry, multiplexer_1_out, nor_1_out, not_1_out, not_2_out, not_3_out, not_4_out, not_5_out,
       or_1_out, or_2_out;
  wire [2:0] LP_q;
  wire [3:0] Licznik_adresowy_q;
  wire [6:0] adder_1_out;
  wire [7:0] adder_3_out, xor_1_out;
  wire [8:0] adder_2_out, REJ_q;
  wire [14:0] rom_1_data;

  Clock CK (.out(CK_out));
  not not_1 (not_1_out, CK_out);
  D_Flip_Flop d_ff_1 (
    .clk(1'b0), .D(1'b0), .Q(ACK), .preset(rom_1_data[10]), .en(1'b0), .reset(rom_1_data[11]));  // open: Qn
  or or_1 (or_1_out, rom_1_data[7], rom_1_data[6]);
  Counter #(.width(3), .max('h7), .ongoal("stay")) LP (
    .load(or_1_out), .D(3'b100), .count(rom_1_data[6]), .Q(LP_q), .clk(CK_out));  // open: carry, clr
  Adder #(.width(7)) adder_1 (
    .a({{4{B[3]}}, B[2:0]}), .b({{2{A[3]}}, A[2:0], 2'b00}), .out(adder_1_out), .cin(1'b0));  // open: cout
  and and_1 (OUT, CK_out, rom_1_data[8]);
  nor nor_1 (nor_1_out, LP_q[0], LP_q[1], LP_q[2]);
  Adder #(.width(9)) adder_2 (
    .a(REJ_q), .b({{3{adder_1_out[6]}}, adder_1_out[5:0]}), .out(adder_2_out), .cin(1'b0));  // open: cout
  Register #(.width(9)) REJ (.D(adder_2_out), .en(rom_1_data[5]), .Q(REJ_q), .clk(CK_out), .clr(rom_1_data[4]));
  not not_2 (not_2_out, nor_1_out);
  not not_3 (not_3_out, SYNC);
  not not_4 (not_4_out, LY_carry);
  Multiplexer #(.select(3), .enable("false")) multiplexer_1 (
    .in0(SYNC), .in1(not_3_out), .in2(not_2_out), .in3(LY_carry), .in4(not_4_out), .in5(1'b1), .in6(1'b0),
    .in7(1'b0), .out(multiplexer_1_out), .sel(rom_1_data[14:12]));
  not not_5 (not_5_out, multiplexer_1_out);
  Counter #(.width(4), .max('hf)) Licznik_adresowy (
    .load(not_5_out), .D(rom_1_data[3:0]), .count(multiplexer_1_out), .Q(Licznik_adresowy_q),
    .clk(not_1_out), .clr(1'b0));  // open: carry
  assign xor_1_out = REJ_q[7:0] ^ {8{REJ_q[8]}};  // XOR_Gate xor_1, 8 bits wide
  Adder adder_3 (.a(xor_1_out), .b({8{1'b0}}), .out(adder_3_out), .cin(REJ_q[8]));  // open: cout
  ROM #(.addrWidth(4), .dataWidth(15)) rom_1 (.addr(Licznik_adresowy_q), .data(rom_1_data), .sel(1'b1));
  or or_2 (or_2_out, rom_1_data[9], rom_1_data[8]);
  Counter LY (.load(or_2_out), .D(adder_3_out), .count(rom_1_data[8]), .carry(LY_carry), .clk(CK_out));  // open: Q, clr

  // Notes on the sheet:
  //   Sterowania
  //   Mikroprogram
  //   contents of rom_1 (hex, n*v repeats v):
  //   5090 801 2065 1403 6001 4207 3106 1407 6000
endmodule
