// Logisim project zadania-01-apn-kpn-quine.circ as structural Verilog: 2 circuits, main circuit main
module main (
);

  wire nand_1_out, nand_2_out, nand_3_out, nand_4_out, nand_5_out, nand_6_out, nor_1_out, nor_2_out,
       nor_3_out, nor_4_out, nor_5_out, nor_6_out, not_1_out, not_2_out, not_3_out, not_4_out, not_5_out,
       not_6_out, not_7_out;

  not not_1 (not_1_out, 1'b0);
  not not_2 (not_2_out, 1'b1);
  not not_3 (not_3_out, 1'b0);
  not not_4 (not_4_out, 1'b0);
  not not_5 (not_5_out, 1'b1);
  not not_6 (not_6_out, 1'b0);
  not not_7 (not_7_out, 1'b0);
  nor nor_1 (nor_1_out, not_2_out, 1'b0);
  nor nor_2 (nor_2_out, 1'b1, not_4_out, 1'b0);
  nor nor_3 (nor_3_out, 1'b0, not_6_out, 1'b0);
  nor nor_4 (nor_4_out, not_2_out, not_6_out, 1'b0);
  nor nor_5 (nor_5_out, not_4_out, 1'b0, not_7_out);
  nand nand_1 (nand_1_out, not_1_out, not_3_out, not_5_out);
  nand nand_2 (nand_2_out, not_1_out, 1'b0, 1'b1);
  nand nand_3 (nand_3_out, 1'b0, 1'b1, 1'b1);
  nand nand_4 (nand_4_out, not_1_out, 1'b1, 1'b1);
  nand nand_5 (nand_5_out, 1'b0, 1'b0, not_5_out);
  nor nor_6 (nor_6_out, nor_1_out, nor_2_out, nor_3_out, nor_4_out, nor_5_out);
  nand nand_6 (nand_6_out, nand_1_out, nand_2_out, nand_3_out, nand_4_out, nand_5_out);
  LED led_1 (.in(nor_6_out));
  LED led_2 (.in(nand_6_out));
endmodule

module _2 (
);

  wire nand_1_out, nand_2_out, nand_3_out, nand_4_out, nand_5_out, nand_6_out, nor_1_out, nor_2_out,
       nor_3_out, nor_4_out, nor_5_out, nor_6_out, not_1_out, not_2_out, not_3_out, not_4_out, not_7_out,
       not_8_out, not_9_out, not_10_out;

  not not_1 (not_1_out, 1'b0);
  not not_2 (not_2_out, 1'b1);
  not not_3 (not_3_out, 1'b0);
  not not_4 (not_4_out, 1'b1);
  // NOT_Gate not_5 has open pins: in=1'b0, out=open
  // NOT_Gate not_6 has open pins: in=1'b1, out=open
  not not_7 (not_7_out, 1'b0);
  not not_8 (not_8_out, 1'b1);
  not not_9 (not_9_out, 1'b0);
  not not_10 (not_10_out, 1'b1);
  nor nor_1 (nor_1_out, not_4_out, not_3_out);
  nor nor_2 (nor_2_out, 1'b1, 1'b0, 1'b1);
  nor nor_3 (nor_3_out, 1'b0, 1'b1, 1'b1);
  nor nor_4 (nor_4_out, 1'b1, 1'b1, 1'b1);
  nor nor_5 (nor_5_out, not_3_out, 1'b1, not_8_out, not_10_out);
  nand nand_1 (nand_1_out, not_1_out, 1'b0);
  nand nand_2 (nand_2_out, not_2_out, 1'b0);
  nand nand_3 (nand_3_out, not_2_out, 1'b0, 1'b0, not_9_out);
  nand nand_4 (nand_4_out, not_2_out, 1'b0, not_7_out, 1'b0);
  nand nand_5 (nand_5_out, 1'b1, not_1_out, 1'b0, 1'b0);
  nand nand_6 (nand_6_out, nand_1_out, nand_2_out, nand_3_out, nand_4_out, nand_5_out);
  nor nor_6 (nor_6_out, nor_1_out, nor_2_out, nor_3_out, nor_4_out, nor_5_out);
  LED led_1 (.in(nor_6_out));
  LED led_2 (.in(nand_6_out));

  // Notes on the sheet:
  //   Punkt 2)
  //   x4
  //   x4
  //   x3
  //   x3
  //   x2
  //   x1
  //   x2
  //   x1
  //   x0
  //   x0
endmodule
