// Logisim project zadania-02-uklady-wielowyjsciowe.circ as structural Verilog: 8 circuits, main circuit Zadanie-A3
module Zadanie_A3 (
  input  in_1,
  input  in_2,
  input  in_3,
  input  in_4,
  input  in_5,
  input  in_6,
  input  in_7,
  input  in_8,
  input  in_9,
  input  in_10,
  output out_11,
  output out_12,
  output out_13,
  output out_14,
  output out_15,
  output out_16,
  output out_17,
  output out_18
);

  wire and_1_out, and_2_out, and_3_out, and_4_out, and_5_out, and_6_out, and_7_out, and_8_out, and_9_out,
       and_10_out, and_11_out, and_12_out, and_13_out, and_14_out, and_15_out, and_16_out, and_17_out,
       and_18_out, and_19_out, and_20_out, and_21_out, and_22_out, and_23_out, and_24_out, not_1_out,
       not_2_out, not_3_out, not_4_out, not_5_out, not_6_out, not_7_out, not_8_out, not_9_out, not_10_out,
       not_11_out, not_12_out, not_13_out, not_14_out, not_15_out, not_16_out, not_17_out, not_18_out,
       not_19_out, not_20_out, not_21_out, not_22_out, not_23_out, not_24_out, or_2_out, or_3_out, or_6_out,
       or_7_out, or_9_out, or_12_out, or_13_out, or_16_out;

  and and_1 (and_1_out, and_4_out, in_1);
  and and_2 (and_2_out, or_2_out, not_1_out);
  not not_1 (not_1_out, in_1);
  or or_1 (out_11, in_1, and_3_out);
  or or_2 (or_2_out, and_4_out, and_5_out);
  not not_2 (not_2_out, and_4_out);
  and and_3 (and_3_out, not_2_out, not_3_out);
  not not_3 (not_3_out, and_5_out);
  and and_4 (and_4_out, and_7_out, in_2);
  and and_5 (and_5_out, or_3_out, not_4_out);
  not not_4 (not_4_out, in_2);
  or or_3 (or_3_out, and_7_out, and_8_out);
  and and_6 (and_6_out, not_5_out, not_6_out);
  or or_4 (out_12, in_2, and_6_out);
  not not_5 (not_5_out, and_7_out);
  not not_6 (not_6_out, and_8_out);
  and and_7 (and_7_out, and_10_out, in_3);
  and and_8 (and_8_out, or_6_out, not_7_out);
  not not_7 (not_7_out, in_3);
  or or_5 (out_13, in_3, and_9_out);
  or or_6 (or_6_out, and_10_out, and_11_out);
  and and_9 (and_9_out, not_8_out, not_9_out);
  not not_8 (not_8_out, and_10_out);
  not not_9 (not_9_out, and_11_out);
  and and_10 (and_10_out, and_13_out, in_4);
  and and_11 (and_11_out, or_7_out, not_10_out);
  not not_10 (not_10_out, in_4);
  or or_7 (or_7_out, and_13_out, and_14_out);
  and and_12 (and_12_out, not_11_out, not_12_out);
  or or_8 (out_14, in_4, and_12_out);
  not not_11 (not_11_out, and_13_out);
  not not_12 (not_12_out, and_14_out);
  and and_13 (and_13_out, and_16_out, in_5);
  and and_14 (and_14_out, or_9_out, not_13_out);
  not not_13 (not_13_out, in_5);
  or or_9 (or_9_out, and_16_out, and_17_out);
  and and_15 (and_15_out, not_14_out, not_15_out);
  or or_10 (out_15, in_5, and_15_out);
  not not_14 (not_14_out, and_16_out);
  not not_15 (not_15_out, and_17_out);
  and and_16 (and_16_out, and_19_out, in_6);
  and and_17 (and_17_out, or_12_out, not_16_out);
  not not_16 (not_16_out, in_6);
  or or_11 (out_16, in_6, and_18_out);
  or or_12 (or_12_out, and_19_out, and_20_out);
  and and_18 (and_18_out, not_17_out, not_18_out);
  not not_17 (not_17_out, and_19_out);
  not not_18 (not_18_out, and_20_out);
  and and_19 (and_19_out, and_22_out, in_7);
  and and_20 (and_20_out, or_13_out, not_19_out);
  not not_19 (not_19_out, in_7);
  or or_13 (or_13_out, and_22_out, and_23_out);
  and and_21 (and_21_out, not_20_out, not_21_out);
  or or_14 (out_17, in_7, and_21_out);
  not not_20 (not_20_out, and_22_out);
  not not_21 (not_21_out, and_23_out);
  and and_22 (and_22_out, in_9, in_8);
  and and_23 (and_23_out, or_16_out, not_22_out);
  not not_22 (not_22_out, in_8);
  or or_15 (out_18, in_8, and_24_out);
  or or_16 (or_16_out, in_9, in_10);
  and and_24 (and_24_out, not_23_out, not_24_out);
  not not_23 (not_23_out, in_9);
  not not_24 (not_24_out, in_10);

  // Notes on the sheet:
  //   A3: przepuszcza pierwszą z prawej grupę zer
endmodule

module Zadanie_A1 (
  input  in_1,
  input  in_2,
  input  in_3,
  input  in_4,
  input  in_5,
  input  in_6,
  input  in_7,
  input  in_8,
  input  in_9,
  input  in_10,
  input  in_11,
  input  in_12,
  input  z0,
  input  p0,
  output out_15,
  output out_16,
  output out_17,
  output out_18,
  output out_19,
  output out_20,
  output out_21,
  output out_22,
  output out_23,
  output out_24,
  output out_25,
  output out_26
);

  wire and_2_out, and_4_out, and_6_out, and_8_out, and_10_out, and_12_out, and_14_out, and_16_out,
       and_18_out, and_20_out, and_22_out, and_24_out, not_1_out, not_2_out, not_3_out, not_4_out, not_5_out,
       not_6_out, not_7_out, not_8_out, not_9_out, not_10_out, not_11_out, not_12_out, or_1_out, or_2_out,
       or_3_out, or_4_out, or_5_out, or_6_out, or_7_out, or_8_out, or_9_out, or_10_out, or_11_out, or_12_out;

  or or_1 (or_1_out, p0, z0);
  and and_1 (out_15, or_1_out, in_1);
  not not_1 (not_1_out, in_1);
  and and_2 (and_2_out, not_1_out, z0);
  or or_2 (or_2_out, out_15, and_2_out);
  not not_2 (not_2_out, in_2);
  and and_3 (out_16, or_2_out, in_2);
  and and_4 (and_4_out, not_2_out, and_2_out);
  or or_3 (or_3_out, out_16, and_4_out);
  not not_3 (not_3_out, in_3);
  and and_5 (out_17, or_3_out, in_3);
  and and_6 (and_6_out, not_3_out, and_4_out);
  or or_4 (or_4_out, out_17, and_6_out);
  and and_7 (out_18, or_4_out, in_4);
  not not_4 (not_4_out, in_4);
  and and_8 (and_8_out, not_4_out, and_6_out);
  or or_5 (or_5_out, out_18, and_8_out);
  and and_9 (out_19, or_5_out, in_5);
  not not_5 (not_5_out, in_5);
  and and_10 (and_10_out, not_5_out, and_8_out);
  or or_6 (or_6_out, out_19, and_10_out);
  and and_11 (out_20, or_6_out, in_6);
  not not_6 (not_6_out, in_6);
  and and_12 (and_12_out, not_6_out, and_10_out);
  or or_7 (or_7_out, out_20, and_12_out);
  and and_13 (out_21, or_7_out, in_7);
  not not_7 (not_7_out, in_7);
  and and_14 (and_14_out, not_7_out, and_12_out);
  or or_8 (or_8_out, out_21, and_14_out);
  and and_15 (out_22, or_8_out, in_8);
  not not_8 (not_8_out, in_8);
  and and_16 (and_16_out, not_8_out, and_14_out);
  or or_9 (or_9_out, out_22, and_16_out);
  and and_17 (out_23, or_9_out, in_9);
  not not_9 (not_9_out, in_9);
  and and_18 (and_18_out, not_9_out, and_16_out);
  or or_10 (or_10_out, out_23, and_18_out);
  not not_10 (not_10_out, in_10);
  and and_19 (out_24, or_10_out, in_10);
  and and_20 (and_20_out, not_10_out, and_18_out);
  or or_11 (or_11_out, out_24, and_20_out);
  not not_11 (not_11_out, in_11);
  and and_21 (out_25, or_11_out, in_11);
  and and_22 (and_22_out, not_11_out, and_20_out);
  or or_12 (or_12_out, out_25, and_22_out);
  and and_23 (out_26, or_12_out, in_12);
  not not_12 (not_12_out, in_12);
  and and_24 (and_24_out, not_12_out, and_22_out);

  // Notes on the sheet:
  //   A1: układ przepuszcający pierwszą z lewej grupę jedynek
endmodule

module Zadanie_A8 (
  input  in_1,
  input  in_2,
  input  in_3,
  input  in_4,
  input  in_5,
  input  in_6,
  input  in_7,
  input  in_8,
  input  in_9,
  input  in_10,
  input  in_11,
  input  in_12,
  input  in_13,
  input  in_14,
  input  in_15,
  input  in_16,
  input  in_17,
  input  in_18,
  input  in_19,
  input  in_20,
  input  in_21,
  input  in_22,
  input  in_23,
  input  in_24,
  input  in_25,
  input  in_26,
  input  in_27,
  input  in_28,
  input  in_29,
  input  in_30,
  input  in_31,
  input  in_32,
  input  in_33,
  input  in_34,
  output out_35,
  output out_36,
  output out_37,
  output out_38,
  output out_39,
  output out_40,
  output out_41,
  output out_42,
  output out_43,
  output out_44,
  output out_45,
  output out_46,
  output out_47,
  output out_48,
  output out_49,
  output out_50
);

  wire or_1_out, or_2_out, or_3_out, or_4_out, or_5_out, or_6_out, or_7_out, or_8_out, or_9_out, or_10_out,
       or_11_out, or_12_out, or_13_out, or_14_out, or_15_out, or_16_out, or_17_out, or_18_out, or_19_out,
       or_20_out, or_21_out, or_22_out, or_23_out, or_24_out, or_25_out, or_26_out, or_27_out, or_28_out,
       or_29_out, or_30_out, or_31_out, or_32_out;

  or or_1 (or_1_out, or_3_out, in_1);
  and and_1 (out_35, in_17, in_34, or_3_out, in_1);
  or or_2 (or_2_out, in_34, in_17);
  or or_3 (or_3_out, or_4_out, in_2);
  and and_2 (out_36, in_18, or_2_out, or_4_out, in_2);
  or or_4 (or_4_out, or_7_out, in_3);
  or or_5 (or_5_out, or_2_out, in_18);
  and and_3 (out_37, in_19, or_5_out, or_7_out, in_3);
  or or_6 (or_6_out, or_5_out, in_19);
  or or_7 (or_7_out, or_9_out, in_4);
  and and_4 (out_38, in_20, or_6_out, or_9_out, in_4);
  or or_8 (or_8_out, or_6_out, in_20);
  or or_9 (or_9_out, or_11_out, in_5);
  and and_5 (out_39, in_21, or_8_out, or_11_out, in_5);
  or or_10 (or_10_out, or_8_out, in_21);
  or or_11 (or_11_out, or_12_out, in_6);
  and and_6 (out_40, in_22, or_10_out, or_12_out, in_6);
  or or_12 (or_12_out, or_15_out, in_7);
  or or_13 (or_13_out, or_10_out, in_22);
  and and_7 (out_41, in_23, or_13_out, or_15_out, in_7);
  or or_14 (or_14_out, or_13_out, in_23);
  or or_15 (or_15_out, or_17_out, in_8);
  and and_8 (out_42, in_24, or_14_out, or_17_out, in_8);
  or or_16 (or_16_out, or_14_out, in_24);
  or or_17 (or_17_out, or_19_out, in_9);
  and and_9 (out_43, in_25, or_16_out, or_19_out, in_9);
  or or_18 (or_18_out, or_16_out, in_25);
  or or_19 (or_19_out, or_20_out, in_10);
  and and_10 (out_44, in_26, or_18_out, or_20_out, in_10);
  or or_20 (or_20_out, or_23_out, in_11);
  or or_21 (or_21_out, or_18_out, in_26);
  and and_11 (out_45, in_27, or_21_out, or_23_out, in_11);
  or or_22 (or_22_out, or_21_out, in_27);
  or or_23 (or_23_out, or_25_out, in_12);
  and and_12 (out_46, in_28, or_22_out, or_25_out, in_12);
  or or_24 (or_24_out, or_22_out, in_28);
  or or_25 (or_25_out, or_27_out, in_13);
  and and_13 (out_47, in_29, or_24_out, or_27_out, in_13);
  or or_26 (or_26_out, or_24_out, in_29);
  or or_27 (or_27_out, or_28_out, in_14);
  and and_14 (out_48, in_30, or_26_out, or_28_out, in_14);
  or or_28 (or_28_out, or_31_out, in_15);
  or or_29 (or_29_out, or_26_out, in_30);
  and and_15 (out_49, in_31, or_29_out, or_31_out, in_15);
  or or_30 (or_30_out, or_29_out, in_31);
  or or_31 (or_31_out, in_33, in_16);
  and and_16 (out_50, in_32, or_30_out, in_33, in_16);
  or or_32 (or_32_out, or_30_out, in_32);

  // Notes on the sheet:
  //   A8: Liczy iloczyn bitów leżących między prawą skrajną jedynką słowa A i lewą skrajną jedynką słowa B
endmodule

module Zadanie_B1 (
  input  x3,
  input  x2,
  input  x1,
  input  x0,
  output y1,
  output y2,
  output y3
);

  wire _0_1_2_3_out, _0_2_4_6_out, _0_2_8_10_out, _5_7_13_15_out, _11__15_out, _13_15_out, not_1_out,
       not_2_out, not_4_out;

  not not_1 (not_1_out, x3);
  not not_2 (not_2_out, x2);
  // NOT_Gate not_3 has open pins: in=x1, out=open
  not not_4 (not_4_out, x0);
  and _0_1_2_3 (_0_1_2_3_out, not_1_out, not_2_out);
  and _13_15 (_13_15_out, x3, x2, x0);
  and _0_2_8_10 (_0_2_8_10_out, not_2_out, not_4_out);
  and _5_7_13_15 (_5_7_13_15_out, x2, x0);
  and _11__15 (_11__15_out, x3, x1, x0);
  and _0_2_4_6 (_0_2_4_6_out, not_1_out, not_4_out);
  or or_1 (y1, _0_1_2_3_out, _13_15_out);
  or or_2 (y2, _0_2_8_10_out, _5_7_13_15_out);
  or or_3 (y3, _5_7_13_15_out, _11__15_out, _0_2_4_6_out);

  // Notes on the sheet:
  //   B1
  //   Minimalizacja łączna: 6x AND, 3x OR
endmodule

module Zadanie_B3 (
  input  x3,
  input  x2,
  input  x1,
  input  x0,
  output y1,
  output y2,
  output y3
);

  wire _0_2_8_10_out, _1_3_5_7_out, _5_7_out, _7_15_out, _8_10_12_14_out, _8_10_out, _9_11_out, not_1_out,
       not_2_out, not_4_out;

  not not_1 (not_1_out, x3);
  not not_2 (not_2_out, x2);
  // NOT_Gate not_3 has open pins: in=x1, out=open
  not not_4 (not_4_out, x0);
  and _8_10 (_8_10_out, x3, not_2_out, not_4_out);
  and _9_11 (_9_11_out, x3, not_2_out, x0);
  and _5_7 (_5_7_out, not_1_out, x2, x0);
  and _1_3_5_7 (_1_3_5_7_out, not_1_out, x0);
  and _8_10_12_14 (_8_10_12_14_out, x3, not_4_out);
  and _0_2_8_10 (_0_2_8_10_out, not_2_out, not_4_out);
  and _7_15 (_7_15_out, x2, x1, x0);
  or or_1 (y1, _8_10_out, _9_11_out, _5_7_out);
  or or_2 (y2, _1_3_5_7_out, _8_10_12_14_out);
  or or_3 (y3, _1_3_5_7_out, _0_2_8_10_out, _7_15_out);

  // Notes on the sheet:
  //   B3
  //   minimalizacja łączna: 7xAND zamiast 8
endmodule

module Zadanie_C1 (
  input  [3:0] x3x2x1x0,
  output out_2
);

  wire multiplexer_1_out;

  Multiplexer #(.select(2), .enable("false")) multiplexer_1 (
    .in0(1'b0), .in1(1'b1), .in2(1'b1), .in3(1'b1), .out(multiplexer_1_out), .sel(x3x2x1x0[2:1]));
  Multiplexer #(.select(2), .enable("false")) multiplexer_2 (
    .in0(1'b1), .in1(x3x2x1x0[2]), .in2(1'b0), .in3(multiplexer_1_out), .out(out_2),
    .sel({x3x2x1x0[3], x3x2x1x0[0]}));
endmodule

module Zadanie_C2 (
  input  [3:0] in_1,
  output out_2
);

  wire multiplexer_1_out;
  wire [1:1] not_1_out;

  not not_1 (not_1_out[1], in_1[2]);
  Multiplexer #(.select(2), .enable("false")) multiplexer_1 (
    .in0(1'b0), .in1(1'b1), .in2(1'b1), .in3(1'b1), .out(multiplexer_1_out), .sel({not_1_out[1], in_1[0]}));
  Multiplexer #(.select(2), .enable("false")) multiplexer_2 (
    .in0(multiplexer_1_out), .in1(in_1[0]), .in2(1'b0), .in3(1'b1), .out(out_2), .sel({in_1[3], in_1[1]}));
endmodule

module Zadanie_C3 (
  input  [3:0] in_1,
  output out_2
);

  wire multiplexer_1_out;
  wire [0:0] not_1_out;

  not not_1 (not_1_out[0], in_1[3]);
  Multiplexer #(.select(2), .enable("false")) multiplexer_1 (
    .in0(1'b0), .in1(1'b1), .in2(1'b1), .in3(1'b1), .out(multiplexer_1_out), .sel({in_1[1], not_1_out[0]}));
  Multiplexer #(.select(2), .enable("false")) multiplexer_2 (
    .in0(1'b1), .in1(not_1_out[0]), .in2(1'b0), .in3(multiplexer_1_out), .out(out_2), .sel({in_1[2], in_1[0]}));
endmodule
