// Logisim project zadania-03-projektowanie-automatow.circ as structural Verilog: 6 circuits, main circuit Zadanie-A1
module Zadanie_A1 (
  output y2,
  output y1,
  output y0
);

  wire and_1_out, clock_1_out, nor_1_out, xor_1_out;

  and and_1 (and_1_out, y1, y0);
  xor xor_1 (xor_1_out, y1, y0);
  nor nor_1 (nor_1_out, y2, y0);
  Clock clock_1 (.out(clock_1_out));
  D_Flip_Flop Q2 (.clk(clock_1_out), .D(and_1_out), .Q(y2), .en(1'b1));  // open: Qn, preset, reset
  D_Flip_Flop Q1 (.clk(clock_1_out), .D(xor_1_out), .Q(y1), .en(1'b1));  // open: Qn, preset, reset
  D_Flip_Flop Q0 (.clk(clock_1_out), .D(nor_1_out), .Q(y0), .en(1'b1));  // open: Qn, preset, reset

  // Notes on the sheet:
  //   Licznik NKB modulo 5
endmodule

module Zadanie_A7 (
  output y_x,
  output y2,
  output y1,
  output y0
);

  wire and_1_out, and_2_out, and_3_out, and_4_out, and_5_out, and_6_out, clock_1_out, or_1_out, or_2_out,
       Q0_qn, Q1_qn, Q2_qn;

  Clock clock_1 (.out(clock_1_out));
  and and_1 (and_1_out, Q2_qn, y1, y0);
  and and_2 (and_2_out, y2, Q0_qn);
  and and_3 (and_3_out, Q2_qn, y0);
  and and_4 (and_4_out, y1, Q0_qn);
  or or_1 (or_1_out, and_1_out, and_2_out);
  or or_2 (or_2_out, and_3_out, and_4_out);
  D_Flip_Flop Q2 (.clk(clock_1_out), .D(or_1_out), .Q(y2), .Qn(Q2_qn), .en(1'b1));  // open: preset, reset
  D_Flip_Flop Q1 (.clk(clock_1_out), .D(or_2_out), .Q(y1), .Qn(Q1_qn), .en(1'b1));  // open: preset, reset
  D_Flip_Flop Q0 (.clk(clock_1_out), .D(Q0_qn), .Q(y0), .Qn(Q0_qn), .en(1'b1));  // open: preset, reset
  and and_5 (and_5_out, Q1_qn, y0);
  and and_6 (and_6_out, y2, y0);
  or or_3 (y_x, and_5_out, and_6_out);

  // Notes on the sheet:
  //   Licznik U2 od -2 do 3
  //   Dodatkowe wyjście y_x sygnalizuje -1 albo 1
endmodule

module Zadanie_A8 (
  output y_x,
  output y2,
  output y1,
  output y0
);

  wire clock_1_out, nand_1_out, nand_2_out, nand_3_out, nand_4_out, nand_5_out, nand_6_out, nand_7_out,
       nand_8_out, nand_9_out, nand_10_out, nand_11_out, nand_12_out, Q0_qn, Q1_qn, Q2_qn;

  Clock clock_1 (.out(clock_1_out));
  nand nand_1 (nand_1_out, y2, Q1_qn, Q0_qn);
  nand nand_2 (nand_2_out, Q2_qn, y0);
  nand nand_3 (nand_3_out, Q2_qn, y1);
  nand nand_4 (nand_4_out, Q1_qn, Q0_qn);
  nand nand_5 (nand_5_out, y1, y0);
  nand nand_6 (nand_6_out, Q1_qn, Q0_qn);
  nand nand_7 (nand_7_out, y1, Q0_qn);
  nand nand_8 (nand_8_out, nand_1_out, nand_2_out, nand_3_out);
  nand nand_9 (nand_9_out, nand_4_out, nand_5_out);
  nand nand_10 (nand_10_out, nand_6_out, nand_7_out);
  D_Flip_Flop Q2 (.clk(clock_1_out), .D(nand_8_out), .Q(y2), .Qn(Q2_qn), .en(1'b1));  // open: preset, reset
  D_Flip_Flop Q1 (.clk(clock_1_out), .D(nand_9_out), .Q(y1), .Qn(Q1_qn), .en(1'b1));  // open: preset, reset
  D_Flip_Flop Q0 (.clk(clock_1_out), .D(nand_10_out), .Q(y0), .Qn(Q0_qn), .en(1'b1));  // open: preset, reset
  nand nand_11 (nand_11_out, y2, Q1_qn, y0);
  nand nand_12 (nand_12_out, Q2_qn, y1, Q0_qn);
  nand nand_13 (y_x, nand_11_out, nand_12_out);

  // Notes on the sheet:
  //   Generuje cyklicznie sekwencje (0, 3, 6, 1, 4, 7, 2, 5)
  //   Sygnalizuje 2 i 5 na dodatkowym wyjściu y_x
endmodule

module Zadanie_B1 (
  input  x,
  input  z,
  output y
);

  wire and_1_out, and_2_out, and_3_out, and_4_out, and_5_out, and_6_out, and_7_out, and_8_out, clock_1_out,
       not_1_out, not_2_out, or_1_out, or_2_out, or_3_out, or_4_out, Q0_q, Q0_qn, Q1_q, Q1_qn, Q2_q, Q2_qn;

  Clock clock_1 (.out(clock_1_out));
  not not_1 (not_1_out, x);
  not not_2 (not_2_out, z);
  and and_1 (and_1_out, Q1_qn, x, not_2_out);
  and and_2 (and_2_out, Q1_q, Q0_qn, not_1_out, not_2_out);
  and and_3 (and_3_out, Q2_q, not_1_out);
  and and_4 (and_4_out, Q2_qn, Q1_qn);
  and and_5 (and_5_out, Q2_q, Q1_q);
  and and_6 (and_6_out, Q2_qn, x);
  or or_1 (or_1_out, and_1_out, and_2_out);
  or or_2 (or_2_out, Q0_q, z, x);
  and and_7 (and_7_out, Q2_qn, not_2_out);
  or or_3 (or_3_out, Q0_q, z, and_3_out);
  and and_8 (and_8_out, Q1_q, not_2_out);
  or or_4 (or_4_out, z, and_4_out, and_5_out, and_6_out);
  J_K_Flip_Flop Q2 (
    .J(or_1_out), .clk(clock_1_out), .K(or_2_out), .Q(Q2_q), .Qn(Q2_qn), .en(1'b1));  // open: preset, reset
  J_K_Flip_Flop Q1 (
    .J(and_7_out), .clk(clock_1_out), .K(or_3_out), .Q(Q1_q), .Qn(Q1_qn), .en(1'b1));  // open: preset, reset
  J_K_Flip_Flop Q0 (
    .J(and_8_out), .clk(clock_1_out), .K(or_4_out), .Q(Q0_q), .Qn(Q0_qn), .en(1'b1));  // open: preset, reset
  and and_9 (y, Q2_qn, Q1_qn, Q0_q);
endmodule

module Zadanie_C1 (
  input  x1,
  input  x0,
  output L1,
  output L0
);

  wire clock_1_out, L0_qn, multiplexer_1_out, multiplexer_2_out;

  Clock clock_1 (.out(clock_1_out));
  Multiplexer #(.select(3), .enable("false")) multiplexer_1 (
    .in0(1'b0), .in1(1'b1), .in2(1'b1), .in3(1'b1), .in4(1'b0), .in5(1'b0), .in6(1'b0), .in7(1'b1),
    .out(multiplexer_1_out), .sel({L1, x1, x0}));
  Multiplexer #(.select(3), .enable("false")) multiplexer_2 (
    .in0(1'b0), .in1(L0_qn), .in2(L0), .in3(1'b0), .in4(1'b0), .in5(L0), .in6(L0_qn), .in7(1'b0),
    .out(multiplexer_2_out), .sel({L1, x1, x0}));
  D_Flip_Flop u_L1 (.clk(clock_1_out), .D(multiplexer_1_out), .Q(L1), .en(1'b1));  // open: Qn, preset, reset
  D_Flip_Flop u_L0 (.clk(clock_1_out), .D(multiplexer_2_out), .Q(L0), .Qn(L0_qn), .en(1'b1));  // open: preset, reset

  // Notes on the sheet:
  //   L1
  //   L0
endmodule

module Wejsciowka (
  output out_1,
  output out_2,
  output out_3,
  output out_4
);

  wire clock_1_out, d_ff_1_qn, j_k_ff_2_qn;

  Clock clock_1 (.out(clock_1_out));
  D_Flip_Flop d_ff_1 (.clk(clock_1_out), .D(d_ff_1_qn), .Q(out_1), .Qn(d_ff_1_qn), .en(1'b1));  // open: preset, reset
  T_Flip_Flop t_ff_1 (.clk(clock_1_out), .T(1'b1), .Q(out_2), .en(1'b1));  // open: Qn, preset, reset
  J_K_Flip_Flop j_k_ff_1 (.J(1'b1), .clk(clock_1_out), .K(1'b1), .Q(out_3), .en(1'b1));  // open: Qn, preset, reset
  J_K_Flip_Flop j_k_ff_2 (
    .J(j_k_ff_2_qn), .clk(clock_1_out), .K(out_4), .Q(out_4), .Qn(j_k_ff_2_qn));  // open: preset, en, reset
endmodule
