// Logisim project zadania-05-automaty-asynchroniczne.circ as structural Verilog
module zadanie_6_sprzezenie_zwrotne (
  input  D,
  input  C,
  output Q
);

  wire nand_1_out, nand_2_out, nand_3_out, nand_4_out, nand_5_out, nand_6_out, not_1_out, Q0_out;

  not not_1 (not_1_out, C);
  nand nand_1 (nand_1_out, not_1_out, Q);
  nand nand_2 (nand_2_out, C, Q0_out);
  nand nand_3 (nand_3_out, Q, Q0_out);
  nand nand_4 (nand_4_out, C, Q0_out);
  nand nand_5 (nand_5_out, D, Q0_out);
  nand nand_6 (nand_6_out, D, not_1_out);
  nand Q1 (Q, nand_1_out, nand_2_out, nand_3_out);
  nand Q0 (Q0_out, nand_4_out, nand_5_out, nand_6_out);
endmodule

module zadanie_6_przerzutniki (
  input  D,
  input  C,
  output out_3
);

  wire not_1_out, not_2_out, or_1_out, or_2_out, or_3_out, or_4_out, Q0_out_3, Q0_out_4;

  not not_1 (not_1_out, D);
  not not_2 (not_2_out, C);
  or or_1 (or_1_out, Q0_out_4, not_2_out, not_1_out);
  or or_2 (or_2_out, not_2_out, Q0_out_3);
  or or_3 (or_3_out, not_1_out, C);
  or or_4 (or_4_out, C, D);
  przerzutnik_nieRnieS Q1 (.nieS(or_1_out), .nieR(or_2_out), .out_3(out_3));  // open: out_4
  przerzutnik_nieRnieS Q0 (.nieS(or_3_out), .nieR(or_4_out), .out_3(Q0_out_3), .out_4(Q0_out_4));
endmodule

module przerzutnik_nieRnieS (
  input  nieS,
  input  nieR,
  output out_3,
  output out_4
);

  wire not_1_out, not_2_out;

  D_Flip_Flop d_ff_1 (.Q(out_3), .Qn(out_4), .preset(not_2_out), .reset(not_1_out));  // open: clk, D, en
  not not_1 (not_1_out, nieR);
  not not_2 (not_2_out, nieS);
endmodule

module wykrywanie_sekwencji (
  input  a,
  input  b,
  output out_3
);

  wire nand_1_out, nand_2_out, nand_3_out, nand_4_out, nand_5_out, nand_6_out, nand_7_out, nand_8_out,
       nand_9_out, nand_10_out, not_1_out, not_2_out, not_3_out, not_4_out, not_5_out;

  not not_1 (not_1_out, a);
  not not_2 (not_2_out, b);
  not not_3 (not_3_out, nand_8_out);
  not not_4 (not_4_out, nand_10_out);
  nand nand_1 (nand_1_out, nand_8_out, a, not_2_out);
  nand nand_2 (nand_2_out, nand_10_out, not_2_out);
  nand nand_3 (nand_3_out, not_1_out, not_2_out);
  nand nand_4 (nand_4_out, nand_9_out, not_4_out, b);
  nand nand_5 (nand_5_out, nand_9_out, not_1_out);
  nand nand_6 (nand_6_out, nand_9_out, a, b);
  nand nand_7 (nand_7_out, not_3_out, nand_10_out, a);
  nand nand_8 (nand_8_out, nand_1_out, nand_2_out);
  nand nand_9 (nand_9_out, nand_3_out, nand_4_out, nand_5_out);
  nand nand_10 (nand_10_out, nand_6_out, nand_7_out);
  and and_1 (out_3, nand_8_out, not_5_out);
  not not_5 (not_5_out, nand_10_out);

  // Notes on the sheet:
  //   Wykrywanie sekwencji 00, 01, 11, 10
endmodule

module swiatla (
  input  a,
  input  b,
  output out_3
);

  wire nand_1_out, nand_2_out, nand_3_out, nand_4_out, nand_5_out, nand_6_out, nand_7_out, nand_8_out,
       not_1_out, not_2_out, not_3_out, not_4_out, not_5_out, not_6_out, Q0_out, Q1_out, Q2_out;

  not not_1 (not_1_out, a);
  not not_2 (not_2_out, b);
  not not_3 (not_3_out, Q2_out);
  not not_4 (not_4_out, Q1_out);
  not not_5 (not_5_out, Q0_out);
  nand nand_1 (nand_1_out, Q2_out, not_2_out);
  nand nand_2 (nand_2_out, not_4_out, Q0_out, not_1_out);
  nand nand_3 (nand_3_out, Q1_out, not_5_out);
  nand nand_4 (nand_4_out, a, b);
  nand nand_5 (nand_5_out, Q2_out, a);
  nand nand_6 (nand_6_out, not_3_out, Q0_out);
  nand nand_7 (nand_7_out, not_3_out, a, not_2_out);
  nand nand_8 (nand_8_out, not_3_out, Q1_out, not_1_out, not_2_out);
  nand Q2 (Q2_out, nand_1_out, nand_2_out);
  nand Q1 (Q1_out, nand_3_out, nand_4_out, nand_5_out);
  nand Q0 (Q0_out, nand_6_out, nand_7_out, nand_8_out);
  and and_1 (out_3, Q1_out, not_6_out);
  not not_6 (not_6_out, Q0_out);
endmodule
